// Logisim project 4 Somador de 8 bits com mais 4.circ as structural Verilog: 2 circuits, main circuit main
module main (
  input  in_1,
  input  _0,
  input  _1,
  input  _2,
  input  _3,
  input  _4,
  input  _5,
  input  _6,
  input  _7,
  output out_10,
  output out_11,
  output out_12,
  output out_13,
  output out_14,
  output out_15,
  output out_16,
  output out_17,
  output out_18
);

  wire somador_1_cout, somador_2_cout, somador_3_cout, somador_4_cout, somador_5_cout, somador_6_cout,
       somador_7_cout;

  somador somador_1 (.A(_0), .B(1'b0), .Cin(in_1), .Cout(somador_1_cout), .Sum(out_11));
  somador somador_2 (.A(_1), .B(1'b0), .Cin(somador_1_cout), .Cout(somador_2_cout), .Sum(out_12));
  somador somador_3 (.A(_2), .B(1'b1), .Cin(somador_2_cout), .Cout(somador_3_cout), .Sum(out_13));
  somador somador_4 (.A(_3), .B(1'b0), .Cin(somador_3_cout), .Cout(somador_4_cout), .Sum(out_14));
  somador somador_5 (.A(_4), .B(1'b0), .Cin(somador_4_cout), .Cout(somador_5_cout), .Sum(out_15));
  somador somador_6 (.A(_5), .B(1'b0), .Cin(somador_5_cout), .Cout(somador_6_cout), .Sum(out_16));
  somador somador_7 (.A(_6), .B(1'b0), .Cin(somador_6_cout), .Cout(somador_7_cout), .Sum(out_17));
  somador somador_8 (.A(_7), .B(1'b0), .Cin(somador_7_cout), .Cout(out_10), .Sum(out_18));
endmodule

module somador (
  input  A,
  input  B,
  input  Cin,
  output Sum,
  output Cout
);

  wire and_1_out, and_2_out, xor_1_out;

  xor xor_1 (xor_1_out, A, B);
  and and_1 (and_1_out, xor_1_out, Cin);
  and and_2 (and_2_out, A, B);
  xor xor_2 (Sum, xor_1_out, Cin);
  or or_1 (Cout, and_1_out, and_2_out);
endmodule
