// Logisim project 5 Memoria ROM.circ as structural Verilog: 2 circuits, main circuit main
module main (
  input  [7:0] in_1,
  input  [7:0] in_2,
  input  [7:0] in_3,
  input  [7:0] in_4,
  input  [7:0] in_5,
  input  [7:0] in_6,
  input  [7:0] in_7,
  input  [7:0] in_8,
  input  [2:0] Select,
  output [7:0] out_10
);

  ROM rom_1 (
    ._0(in_1), ._1(in_2), ._2(in_3), ._3(in_4), ._4(in_5), ._5(in_6), ._6(in_7), ._7(in_8), .Select(Select),
    .out_10(out_10));
endmodule

module ROM (
  input  [7:0] _0,
  input  [7:0] _1,
  input  [7:0] _2,
  input  [7:0] _3,
  input  [7:0] _4,
  input  [7:0] _5,
  input  [7:0] _6,
  input  [7:0] _7,
  input  [2:0] Select,
  output [7:0] out_10
);

  multiplexador_8_bits multiplexador_8_bits_1 (
    .AND(_0), .OR(_1), .NOT(_2), .NOR(_3), .NAND(_4), .XOR(_5), .SHIFT_ESQ(_6), .SHIFT_DIR(_7),
    .SOMA({8{1'b0}}), .SUB({8{1'b0}}), .Cod({1'b0, Select}), .Out(out_10));
endmodule
